// Logisim project Actividad 1_circuito simplificado.circ as structural Verilog: 1 circuit, main circuit main
module main (
  input  A,
  input  B,
  input  C
);

  wire and_1_out, or_1_out;

  and and_1 (and_1_out, B, C);
  or or_1 (or_1_out, A, and_1_out);
  LED led_1 (.in(or_1_out));
endmodule
