// Logisim project Actividad 2 nuevo sistema.circ as structural Verilog: 1 circuit, main circuit main
module main (
  input  A,
  input  B,
  input  C,
  input  D
);

  wire and_1_out, and_2_out, or_1_out, or_2_out, or_3_out, xor_1_out;

  or or_1 (or_1_out, C, D);
  and and_1 (and_1_out, B, C, D);
  and and_2 (and_2_out, B, or_1_out);
  or or_2 (or_2_out, A, and_2_out);
  or or_3 (or_3_out, A, and_1_out);
  xor xor_1 (xor_1_out, C, D);
  LED ALARMA (.in(or_2_out));
  LED ASPERSORES (.in(or_3_out));
  LED LED_INDICADOR (.in(xor_1_out));
endmodule
