// Logisim project Actividad 2 un solo tipo de compuerta.circ as structural Verilog: 1 circuit, main circuit main
module main (
  input  A,
  input  B,
  input  C,
  input  D
);

  wire nand_1_out, nand_2_out, nand_3_out, nand_4_out, nand_5_out, nand_6_out, nand_7_out, nand_8_out,
       nand_9_out, nand_10_out, nand_11_out, nand_12_out, nand_13_out, nand_14_out, nand_15_out, nand_16_out,
       nand_17_out;

  nand nand_1 (nand_1_out, C, C);
  nand nand_2 (nand_2_out, D, D);
  nand nand_3 (nand_3_out, nand_1_out, nand_2_out);
  nand nand_4 (nand_4_out, B, C, D);
  nand nand_5 (nand_5_out, nand_4_out, nand_4_out, nand_4_out);
  nand nand_6 (nand_6_out, B, nand_3_out);
  nand nand_7 (nand_7_out, nand_6_out, nand_6_out);
  nand nand_8 (nand_8_out, C, D);
  nand nand_9 (nand_9_out, A, A);
  nand nand_10 (nand_10_out, nand_7_out, nand_7_out);
  nand nand_11 (nand_11_out, A, A);
  nand nand_12 (nand_12_out, nand_5_out, nand_5_out);
  nand nand_13 (nand_13_out, C, nand_8_out);
  nand nand_14 (nand_14_out, nand_8_out, D);
  nand nand_15 (nand_15_out, nand_9_out, nand_10_out);
  nand nand_16 (nand_16_out, nand_11_out, nand_12_out);
  nand nand_17 (nand_17_out, nand_13_out, nand_14_out);
  LED ALARMA (.in(nand_15_out));
  LED ASPERSORES (.in(nand_16_out));
  LED LED_INDICADOR (.in(nand_17_out));
endmodule
