// Logisim project ALU.circ as structural Verilog
module main (
  input  A,
  input  B,
  input  Cin,
  output Sum,
  output Cout
);

  Multiplexer #(.select(3)) multiplexer_1 (
    .in0(1'b0), .in1(1'b0), .in2(1'b0), .in3(1'b1), .in4(1'b0), .in5(1'b1), .in6(1'b1), .in7(1'b1),
    .out(Cout), .sel({Cin, B, A}), .en(1'b1));
  Multiplexer #(.select(3)) multiplexer_2 (
    .in0(1'b0), .in1(1'b1), .in2(1'b1), .in3(1'b0), .in4(1'b1), .in5(1'b0), .in6(1'b0), .in7(1'b1),
    .out(Sum), .sel({Cin, B, A}), .en(1'b1));
endmodule

module _4Bit_Adder (
  input  A3,
  input  A2,
  input  A1,
  input  A0,
  input  B3,
  input  B2,
  input  B1,
  input  B0,
  input  Resta,
  output out_10,
  output out_11,
  output out_12,
  output out_13,
  output out_14
);

  wire main_1_cout, main_2_cout, main_3_cout, xor_1_out, xor_2_out, xor_3_out, xor_4_out;

  xor xor_1 (xor_1_out, Resta, B0);
  main main_1 (.A(A0), .B(xor_1_out), .Cin(Resta), .Sum(out_11), .Cout(main_1_cout));
  xor xor_2 (xor_2_out, Resta, B1);
  main main_2 (.A(A1), .B(xor_2_out), .Cin(main_1_cout), .Sum(out_12), .Cout(main_2_cout));
  main main_3 (.A(A2), .B(xor_3_out), .Cin(main_2_cout), .Sum(out_13), .Cout(main_3_cout));
  xor xor_3 (xor_3_out, Resta, B2);
  xor xor_4 (xor_4_out, Resta, B3);
  main main_4 (.A(A3), .B(xor_4_out), .Cin(main_3_cout), .Sum(out_14), .Cout(out_10));
endmodule

module ALU (
  input  A0,
  input  A1,
  input  F0,
  input  A2,
  input  F1,
  input  A3,
  input  F2,
  input  B0,
  input  B1,
  input  B2,
  input  B3,
  output [3:0] out_12,
  output out_13
);

  wire [3:0] adder_1_out, and_1_out, bit_extender_1_out, or_1_out, subtractor_1_out;

  assign and_1_out = {A0, A1, A2, A3} & {B0, B1, B2, B3};  // AND_Gate and_1, 4 bits wide
  assign or_1_out = {A0, A1, A2, A3} | {B0, B1, B2, B3};  // OR_Gate or_1, 4 bits wide
  Adder #(.width(4)) adder_1 (.a({A0, A1, A2, A3}), .b({B0, B1, B2, B3}), .out(adder_1_out));  // open: cin, cout
  Subtractor #(.width(4)) subtractor_1 (
    .a({A0, A1, A2, A3}), .b({B0, B1, B2, B3}), .out(subtractor_1_out));  // open: bin, bout
  Comparator #(.width(4)) comparator_1 (.a({A0, A1, A2, A3}), .b({B0, B1, B2, B3}), .lt(out_13));  // open: gt, eq
  assign bit_extender_1_out = {{3{1'b0}}, out_13};  // Bit_Extender bit_extender_1
  LED B_A (.in(out_13));
  Multiplexer #(.select(3), .width(4)) multiplexer_1 (
    .in0(and_1_out), .in1(and_1_out), .in2(or_1_out), .in3(adder_1_out), .in4(bit_extender_1_out),
    .in5(subtractor_1_out), .in6(bit_extender_1_out), .in7(subtractor_1_out), .out(out_12),
    .sel({F0, F1, F2}), .en(1'b1));
endmodule

module dec1 (
  input  A0,
  input  A1,
  input  A2,
  input  A3,
  output a,
  output b,
  output c,
  output d,
  output e,
  output f,
  output g
);

  wire and_1_out, and_2_out, and_3_out, and_4_out, not_1_out, not_2_out, not_3_out, not_4_out, not_5_out,
       not_6_out, not_7_out, not_8_out, not_9_out, not_10_out, not_11_out, not_12_out;

  not not_1 (not_1_out, A0);
  not not_2 (not_2_out, A1);
  and and_1 (and_1_out, not_2_out, not_3_out);
  not not_3 (not_3_out, A2);
  not not_4 (not_4_out, A0);
  not not_5 (not_5_out, A1);
  and and_2 (and_2_out, not_5_out, not_6_out);
  not not_6 (not_6_out, A2);
  not not_7 (not_7_out, A0);
  not not_8 (not_8_out, A1);
  and and_3 (and_3_out, not_8_out, not_9_out);
  not not_9 (not_9_out, A2);
  not not_10 (not_10_out, A0);
  not not_11 (not_11_out, A1);
  and and_4 (and_4_out, not_11_out, not_12_out);
  not not_12 (not_12_out, A2);
  or or_1 (a, not_1_out, and_1_out);
  or or_2 (d, not_4_out, and_2_out);
  or or_3 (e, not_7_out, and_3_out);
  or or_4 (f, not_10_out, and_4_out);

  assign b = 1'b1;
  assign c = 1'b1;
  assign g = 1'b0;
endmodule

module dec2 (
  input  A0,
  input  A1,
  input  A2,
  input  A3,
  output a,
  output b,
  output c,
  output d,
  output e,
  output f,
  output g
);

  wire and_1_out, and_2_out, and_3_out, and_4_out, and_5_out, and_6_out, and_7_out, and_8_out, and_9_out,
       and_10_out, and_11_out, and_12_out, and_13_out, and_14_out, and_15_out, and_16_out, and_17_out,
       and_18_out, and_19_out, and_20_out, and_21_out, and_22_out, and_23_out, and_24_out, and_25_out,
       and_26_out, and_27_out, and_28_out, and_29_out, and_30_out, and_31_out, not_1_out, not_2_out,
       not_3_out, not_4_out, not_5_out, not_6_out, not_7_out, not_8_out, not_9_out, not_10_out, not_11_out,
       not_12_out, not_13_out, not_14_out, not_15_out, not_16_out, not_17_out, not_18_out, not_19_out,
       not_20_out, not_21_out, not_22_out, not_23_out, not_24_out, not_25_out, not_26_out, not_27_out,
       not_28_out, not_29_out, not_30_out, not_31_out, not_32_out, not_33_out, not_34_out, not_35_out,
       not_36_out, not_37_out, not_38_out, not_39_out, not_40_out, not_41_out, not_42_out, not_43_out,
       not_44_out;

  not not_1 (not_1_out, A1);
  and and_1 (and_1_out, not_1_out, not_2_out);
  not not_2 (not_2_out, A3);
  not not_3 (not_3_out, A0);
  and and_2 (and_2_out, not_3_out, A2);
  and and_3 (and_3_out, A1, A3);
  and and_4 (and_4_out, A0, not_4_out);
  not not_4 (not_4_out, A2);
  not not_5 (not_5_out, A1);
  not not_6 (not_6_out, A2);
  and and_5 (and_5_out, not_6_out, not_7_out);
  not not_7 (not_7_out, A3);
  not not_8 (not_8_out, A0);
  and and_6 (and_6_out, not_8_out, A2, A3);
  and and_7 (and_7_out, A0, not_9_out);
  not not_9 (not_9_out, A2);
  and and_8 (and_8_out, A0, not_10_out);
  not not_10 (not_10_out, A3);
  not not_11 (not_11_out, A0);
  and and_9 (and_9_out, not_11_out, not_12_out);
  not not_12 (not_12_out, A2);
  and and_10 (and_10_out, A1, A2);
  and and_11 (and_11_out, A0, not_13_out);
  not not_13 (not_13_out, A1);
  not not_14 (not_14_out, A1);
  and and_12 (and_12_out, not_14_out, not_15_out);
  not not_15 (not_15_out, A3);
  not not_16 (not_16_out, A0);
  and and_13 (and_13_out, not_16_out, not_17_out, A2);
  not not_17 (not_17_out, A1);
  not not_18 (not_18_out, A0);
  and and_14 (and_14_out, not_18_out, A2, not_19_out);
  not not_19 (not_19_out, A3);
  not not_20 (not_20_out, A2);
  and and_15 (and_15_out, A1, not_20_out, A3);
  not not_21 (not_21_out, A2);
  and and_16 (and_16_out, A0, not_21_out, not_22_out);
  not not_22 (not_22_out, A3);
  and and_17 (and_17_out, A0, A1, A3);
  not not_23 (not_23_out, A1);
  and and_18 (and_18_out, not_23_out, not_24_out);
  not not_24 (not_24_out, A3);
  not not_25 (not_25_out, A0);
  and and_19 (and_19_out, not_25_out, A2, not_26_out);
  not not_26 (not_26_out, A3);
  not not_27 (not_27_out, A2);
  and and_20 (and_20_out, A0, not_27_out, not_28_out);
  not not_28 (not_28_out, A3);
  not not_29 (not_29_out, A0);
  not not_30 (not_30_out, A2);
  and and_21 (and_21_out, not_29_out, not_30_out, not_31_out);
  not not_31 (not_31_out, A3);
  not not_32 (not_32_out, A0);
  and and_22 (and_22_out, not_32_out, A1, not_33_out);
  not not_33 (not_33_out, A2);
  not not_34 (not_34_out, A0);
  and and_23 (and_23_out, not_34_out, A1, not_35_out);
  not not_35 (not_35_out, A3);
  not not_36 (not_36_out, A1);
  and and_24 (and_24_out, A0, not_36_out, not_37_out);
  not not_37 (not_37_out, A2);
  not not_38 (not_38_out, A1);
  and and_25 (and_25_out, A0, not_38_out, not_39_out);
  not not_39 (not_39_out, A3);
  and and_26 (and_26_out, A0, A1, A2);
  not not_40 (not_40_out, A0);
  and and_27 (and_27_out, not_40_out, not_41_out, A2);
  not not_41 (not_41_out, A1);
  and and_28 (and_28_out, A1, not_42_out);
  not not_42 (not_42_out, A2);
  and and_29 (and_29_out, A1, not_43_out);
  not not_43 (not_43_out, A3);
  and and_30 (and_30_out, A0, not_44_out);
  not not_44 (not_44_out, A2);
  and and_31 (and_31_out, A0, A1);
  or or_1 (a, and_1_out, and_2_out, and_3_out, and_4_out);
  or or_2 (b, not_5_out, and_5_out, and_6_out, and_7_out, and_8_out);
  or or_3 (c, and_9_out, A3, and_10_out, and_11_out);
  or or_4 (e, and_18_out, and_19_out, and_20_out);
  or or_5 (g, and_27_out, and_28_out, and_29_out, and_30_out, and_31_out);
  or or_6 (d, and_12_out, and_13_out, and_14_out, and_15_out, and_16_out, and_17_out);
  or or_7 (f, and_21_out, and_22_out, and_23_out, and_24_out, and_25_out, and_26_out);
endmodule

module displays (
  input  A0,
  input  A1,
  input  A2,
  input  A3
);

  wire dec1_1_a, dec1_1_b, dec1_1_c, dec1_1_d, dec1_1_e, dec1_1_f, dec1_1_g, dec2_1_a, dec2_1_b, dec2_1_c,
       dec2_1_d, dec2_1_e, dec2_1_f, dec2_1_g;

  dec1 dec1_1 (
    .A0(A0), .A1(A1), .A2(A2), .A3(A3), .a(dec1_1_a), .b(dec1_1_b), .c(dec1_1_c), .d(dec1_1_d), .e(dec1_1_e),
    .f(dec1_1_f), .g(dec1_1_g));
  _7_Segment_Display u_7_segment_display_1 (
    .g(dec1_1_g), .f(dec1_1_f), .a(dec1_1_a), .b(dec1_1_b), .e(dec1_1_e), .d(dec1_1_d), .c(dec1_1_c));  // open: dp
  _7_Segment_Display u_7_segment_display_2 (
    .g(dec2_1_g), .f(dec2_1_f), .a(dec2_1_a), .b(dec2_1_b), .e(dec2_1_e), .d(dec2_1_d), .c(dec2_1_c));  // open: dp
  dec2 dec2_1 (
    .A0(A0), .A1(A1), .A2(A2), .A3(A3), .a(dec2_1_a), .b(dec2_1_b), .c(dec2_1_c), .d(dec2_1_d), .e(dec2_1_e),
    .f(dec2_1_f), .g(dec2_1_g));
endmodule

module jkbhj (
  input  A0,
  input  A1,
  input  A2,
  input  A3,
  input  F0,
  input  F1,
  input  F2,
  input  B0,
  input  B1,
  input  B2,
  input  B3,
  output [3:0] out_12
);

  wire alu_1_out_13, dec1_1_a, dec1_1_b, dec1_1_c, dec1_1_d, dec1_1_e, dec1_1_f, dec1_1_g, dec1_2_a,
       dec1_2_b, dec1_2_c, dec1_2_d, dec1_2_e, dec1_2_f, dec1_2_g, dec2_1_a, dec2_1_b, dec2_1_c, dec2_1_d,
       dec2_1_e, dec2_1_f, dec2_1_g, dec2_2_a, dec2_2_b, dec2_2_c, dec2_2_d, dec2_2_e, dec2_2_f, dec2_2_g;

  dec1 dec1_1 (
    .A0(A0), .A1(A1), .A2(A2), .A3(A3), .a(dec1_1_a), .b(dec1_1_b), .c(dec1_1_c), .d(dec1_1_d), .e(dec1_1_e),
    .f(dec1_1_f), .g(dec1_1_g));
  dec1 dec1_2 (
    .A0(B0), .A1(B1), .A2(B2), .A3(B3), .a(dec1_2_a), .b(dec1_2_b), .c(dec1_2_c), .d(dec1_2_d), .e(dec1_2_e),
    .f(dec1_2_f), .g(dec1_2_g));
  _7_Segment_Display u_7_segment_display_1 (
    .g(dec1_1_g), .f(dec1_1_f), .a(dec1_1_a), .b(dec1_1_b), .e(dec1_1_e), .d(dec1_1_d), .c(dec1_1_c));  // open: dp
  _7_Segment_Display u_7_segment_display_2 (
    .g(dec2_1_g), .f(dec2_1_f), .a(dec2_1_a), .b(dec2_1_b), .e(dec2_1_e), .d(dec2_1_d), .c(dec2_1_c));  // open: dp
  _7_Segment_Display u_7_segment_display_3 (
    .g(dec1_2_g), .f(dec1_2_f), .a(dec1_2_a), .b(dec1_2_b), .e(dec1_2_e), .d(dec1_2_d), .c(dec1_2_c));  // open: dp
  _7_Segment_Display u_7_segment_display_4 (
    .g(dec2_2_g), .f(dec2_2_f), .a(dec2_2_a), .b(dec2_2_b), .e(dec2_2_e), .d(dec2_2_d), .c(dec2_2_c));  // open: dp
  dec2 dec2_1 (
    .A0(A0), .A1(A1), .A2(A2), .A3(A3), .a(dec2_1_a), .b(dec2_1_b), .c(dec2_1_c), .d(dec2_1_d), .e(dec2_1_e),
    .f(dec2_1_f), .g(dec2_1_g));
  dec2 dec2_2 (
    .A0(B0), .A1(B1), .A2(B2), .A3(B3), .a(dec2_2_a), .b(dec2_2_b), .c(dec2_2_c), .d(dec2_2_d), .e(dec2_2_e),
    .f(dec2_2_f), .g(dec2_2_g));
  ALU alu_1 (
    .B0(B0), .B1(B1), .B2(B2), .B3(B3), .F0(F0), .F1(F1), .F2(F2), .out_12(out_12), .out_13(alu_1_out_13),
    .A0(A0), .A1(A1), .A2(A2), .A3(A3));
  Hex_Digit_Display hex_digit_display_1 (.value(out_12));  // open: dp
  LED led_1 (.in(alu_1_out_13));
endmodule
