// Logisim project lab3.circ as structural Verilog: 3 circuits, main circuit main
module main (
);

  wire and_1_out, clock_1_out, d_ff_2_q, d_ff_2_qn, d_ff_3_q, d_ff_3_qn, j_k_ff_1_q, j_k_ff_2_q, j_k_ff_3_q;

  D_Flip_Flop d_ff_1 ();  // open: clk, D, Q, Qn, preset, en, reset
  Clock clock_1 (.out(clock_1_out));
  J_K_Flip_Flop j_k_ff_1 (.J(1'b1), .clk(clock_1_out), .K(1'b1), .Q(j_k_ff_1_q));  // open: Qn, preset, en, reset
  J_K_Flip_Flop j_k_ff_2 (.J(1'b1), .clk(j_k_ff_1_q), .K(1'b1), .Q(j_k_ff_2_q));  // open: Qn, preset, en, reset
  D_Flip_Flop d_ff_2 (.clk(clock_1_out), .D(d_ff_2_qn), .Q(d_ff_2_q), .Qn(d_ff_2_qn));  // open: preset, en, reset
  D_Flip_Flop d_ff_3 (.clk(d_ff_2_qn), .D(d_ff_3_qn), .Q(d_ff_3_q), .Qn(d_ff_3_qn));  // open: preset, en, reset
  J_K_Flip_Flop j_k_ff_3 (.J(1'b1), .clk(j_k_ff_2_q), .K(1'b1), .Q(j_k_ff_3_q));  // open: Qn, preset, en, reset
  J_K_Flip_Flop j_k_ff_4 (.J(1'b1), .clk(j_k_ff_3_q), .K(1'b1));  // open: Q, Qn, preset, en, reset
  and and_1 (and_1_out, d_ff_2_qn, d_ff_3_q);
  LED led_1 (.in(d_ff_3_qn));
  LED led_2 (.in(d_ff_2_q));
  LED led_3 (.in(and_1_out));
endmodule

module XD (
);

  wire clock_1_out, colores_1_a, colores_1_r, colores_1_v, d_ff_1_q, d_ff_1_qn, d_ff_2_q, d_ff_2_qn,
       d_ff_3_q, d_ff_3_qn, d_ff_4_q, d_ff_4_qn, d_ff_5_q, d_ff_5_qn;

  Clock clock_1 (.out(clock_1_out));
  D_Flip_Flop d_ff_1 (
    .clk(clock_1_out), .D(d_ff_1_qn), .Q(d_ff_1_q), .Qn(d_ff_1_qn), .en(1'b1));  // open: preset, reset
  D_Flip_Flop d_ff_2 (.clk(d_ff_1_q), .D(d_ff_2_qn), .Q(d_ff_2_q), .Qn(d_ff_2_qn), .en(1'b1));  // open: preset, reset
  COLORES colores_1 (
    .A4(d_ff_5_q), .A3(d_ff_4_q), .A2(d_ff_3_q), .A1(d_ff_2_q), .A0(d_ff_1_q), .V(colores_1_v),
    .A(colores_1_a), .R(colores_1_r));
  LED led_1 (.in(colores_1_a));
  LED led_2 (.in(colores_1_v));
  LED led_3 (.in(colores_1_r));
  D_Flip_Flop d_ff_3 (.clk(d_ff_2_q), .D(d_ff_3_qn), .Q(d_ff_3_q), .Qn(d_ff_3_qn), .en(1'b1));  // open: preset, reset
  D_Flip_Flop d_ff_4 (.clk(d_ff_3_q), .D(d_ff_4_qn), .Q(d_ff_4_q), .Qn(d_ff_4_qn), .en(1'b1));  // open: preset, reset
  D_Flip_Flop d_ff_5 (.clk(d_ff_4_q), .D(d_ff_5_qn), .Q(d_ff_5_q), .Qn(d_ff_5_qn), .en(1'b1));  // open: preset, reset
endmodule

module COLORES (
  input  A4,
  input  A3,
  input  A2,
  input  A1,
  input  A0,
  output V,
  output A,
  output R
);

  wire and_1_out, and_2_out, and_3_out, and_4_out, and_5_out, not_1_out, not_2_out, not_3_out, not_4_out,
       not_5_out, not_6_out, not_7_out, not_8_out, not_9_out;

  not not_1 (not_1_out, A4);
  not not_2 (not_2_out, A4);
  not not_3 (not_3_out, A4);
  not not_4 (not_4_out, A3);
  not not_5 (not_5_out, A2);
  not not_6 (not_6_out, A1);
  not not_7 (not_7_out, A3);
  not not_8 (not_8_out, A2);
  not not_9 (not_9_out, A0);
  and and_1 (and_1_out, not_1_out, A1, A0);
  and and_2 (and_2_out, not_2_out, A2);
  and and_3 (and_3_out, not_3_out, A3);
  and and_4 (and_4_out, not_4_out, not_5_out, not_6_out);
  and and_5 (and_5_out, not_7_out, not_8_out, not_9_out);
  or or_1 (V, and_1_out, and_2_out, and_3_out);
  or or_2 (A, and_4_out, and_5_out);

  assign R = A4;
endmodule
